// Logisim project Proj 4.circ as structural Verilog: 24 circuits, main circuit main
module main (
  input  in_1,
  input  in_2,
  input  in_3,
  input  in_4,
  input  in_5,
  input  in_6,
  input  in_7,
  input  in_8,
  input  in_9,
  input  in_10
);

  wire bubble, clkdivider_1_out_3, clock_1_out, cmpout, controller_1_immsel, controller_1_isload,
       controller_1_isstore, controller_1_regwrten, pipeline_reg_1_isloadout, pipeline_reg_1_isstoreout,
       pipeline_reg_1_regwrtenout, RST_out;
  wire [1:0] controller_1_memoutsel, pcsel, pipeline_reg_1_memselout;
  wire [3:0] controller_1_rd, datamemory_1_hex, datamemory_1_hex_2, datamemory_1_hex_3, datamemory_1_hex_4,
       keys, pipeline_reg_1_rd_2, rs1, rs2;
  wire [4:0] controller_1_sndop;
  wire [7:0] datamemory_1_ledg;
  wire [9:0] datamemory_1_ledr;
  wire [31:0] adder_1_out, alu_1_dataout, branchaddrcalculator_1_braddr, datamemory_1_dout, ir_1_dout,
       multiplexer_1_out, multiplexer_2_out, multiplexer_3_out, pc_1_out_4, pipeline_reg_1_aluoutout,
       pipeline_reg_1_dataout2out, pipeline_reg_1_nxtpc, register_file_1_data1, register_file_1_data2, seimm;

  Clock clock_1 (.out(clock_1_out));
  Button RST (.out(RST_out));
  BranchAddrCalculator branchaddrcalculator_1 (
    .nxtPC(adder_1_out), .seImm(seimm), .brAddr(branchaddrcalculator_1_braddr));
  Multiplexer #(.select(2), .width(32), .enable("false")) multiplexer_1 (
    .in0(adder_1_out), .in1(branchaddrcalculator_1_braddr), .in2(alu_1_dataout), .in3(pc_1_out_4),
    .out(multiplexer_1_out), .sel(pcsel));
  ClkDivider clkdivider_1 (.CLK(clock_1_out), .RST(RST_out), .out_3(clkdivider_1_out_3));
  PC pc_1 (.in_1(multiplexer_1_out), .CLK(clkdivider_1_out_3), .RST(RST_out), .out_4(pc_1_out_4));
  Adder #(.width(32)) adder_1 (.a(32'h4), .b(pc_1_out_4), .out(adder_1_out));  // open: cin, cout
  IR ir_1 (.pcIn(pc_1_out_4[10:0]), .dOut(ir_1_dout));
  Register_File register_file_1 (
    .RS1(rs1), .RS2(rs2), .EN(pipeline_reg_1_regwrtenout), .RD(pipeline_reg_1_rd_2),
    .DataIn(multiplexer_3_out), .CLK(clkdivider_1_out_3), .RST(RST_out), .Data1(register_file_1_data1),
    .Data2(register_file_1_data2));
  Hex_Digit_Display hex_digit_display_1 (.value(datamemory_1_hex_4));  // open: dp
  Hex_Digit_Display hex_digit_display_2 (.value(datamemory_1_hex_3));  // open: dp
  Controller controller_1 (
    .iWord(ir_1_dout), .memOutSel(controller_1_memoutsel), .RegWrtEn(controller_1_regwrten),
    .isStore(controller_1_isstore), .RD(controller_1_rd), .RS2(rs2), .RS1(rs1), .sndOp(controller_1_sndop),
    .SeImm(seimm), .immsel(controller_1_immsel), .pcSel(pcsel), .ALUcmpIn(cmpout),
    .isLoad(controller_1_isload), .bubble(bubble));
  Hex_Digit_Display hex_digit_display_3 (.value(datamemory_1_hex_2));  // open: dp
  Hex_Digit_Display hex_digit_display_4 (.value(datamemory_1_hex));  // open: dp
  ALU alu_1 (
    .in_1(register_file_1_data1), .in_2(multiplexer_2_out), .DataOut(alu_1_dataout), .cmpOut(cmpout),
    .in_3(controller_1_sndop));
  Multiplexer #(.width(32), .enable("false")) multiplexer_2 (
    .in0(register_file_1_data2), .in1(seimm), .out(multiplexer_2_out), .sel(controller_1_immsel));
  bubbler bubbler_1 (
    .prevWrEn(pipeline_reg_1_regwrtenout), .rs1(rs1), .rs2(rs2), .prevrd(pipeline_reg_1_rd_2), .bubble(bubble));
  LED led_1 (.in(datamemory_1_ledr[8]));
  LED led_2 (.in(datamemory_1_ledr[7]));
  LED led_3 (.in(datamemory_1_ledr[9]));
  LED led_4 (.in(datamemory_1_ledr[6]));
  LED led_5 (.in(datamemory_1_ledr[4]));
  LED led_6 (.in(datamemory_1_ledr[3]));
  LED led_7 (.in(datamemory_1_ledr[5]));
  LED led_8 (.in(datamemory_1_ledr[1]));
  LED led_9 (.in(datamemory_1_ledr[2]));
  LED led_10 (.in(datamemory_1_ledr[0]));
  LED led_11 (.in(datamemory_1_ledg[6]));
  LED led_12 (.in(datamemory_1_ledg[7]));
  LED led_13 (.in(datamemory_1_ledg[5]));
  Pipeline_Reg pipeline_reg_1 (
    .PCinc(adder_1_out), .DataOut2(register_file_1_data2), .CLK(clkdivider_1_out_3),
    .nxtPC(pipeline_reg_1_nxtpc), .DataOut2Out(pipeline_reg_1_dataout2out), .RST(RST_out),
    .memSel(controller_1_memoutsel), .memSelOut(pipeline_reg_1_memselout), .RegWrtEn(controller_1_regwrten),
    .isStore(controller_1_isstore), .RegWrtEnOut(pipeline_reg_1_regwrtenout),
    .isStoreOut(pipeline_reg_1_isstoreout), .rd(controller_1_rd), .rd_2(pipeline_reg_1_rd_2),
    .aluOut(alu_1_dataout), .AluOutOut(pipeline_reg_1_aluoutout), .isLoad(controller_1_isload),
    .isLoadOut(pipeline_reg_1_isloadout));
  LED led_14 (.in(datamemory_1_ledg[3]));
  LED led_15 (.in(datamemory_1_ledg[4]));
  LED led_16 (.in(datamemory_1_ledg[2]));
  LED led_17 (.in(datamemory_1_ledg[1]));
  Button button_1 (.out(keys[3]));
  LED led_18 (.in(datamemory_1_ledg[0]));
  DataMemory datamemory_1 (
    .ADDR(pipeline_reg_1_aluoutout), .Din(pipeline_reg_1_dataout2out), .str(pipeline_reg_1_isstoreout),
    .ld(pipeline_reg_1_isloadout), .Sw({in_1, in_2, in_3, in_4, in_5, in_6, in_7, in_8, in_9, in_10}),
    .Key(keys), .CLK(clkdivider_1_out_3), .RST(RST_out), .Dout(datamemory_1_dout),
    .HEX({datamemory_1_hex_4, datamemory_1_hex_3, datamemory_1_hex_2, datamemory_1_hex}),
    .LEDR(datamemory_1_ledr), .LEDG(datamemory_1_ledg));
  Button button_2 (.out(keys[2]));
  Button button_3 (.out(keys[0]));
  Button button_4 (.out(keys[1]));
  Multiplexer #(.select(2), .width(32), .enable("false")) multiplexer_3 (
    .in0(pipeline_reg_1_aluoutout), .in1(datamemory_1_dout), .in2(pipeline_reg_1_nxtpc), .in3({32{1'b0}}),
    .out(multiplexer_3_out), .sel(pipeline_reg_1_memselout));

  // Other names for the same wires on the sheet: switches[9:0] = {in_1, in_2, in_3, in_4, in_5, in_6, in_7, in_8, in_9, in_10}
endmodule

// PR
module Pipeline_Reg (
  input  [31:0] PCinc,
  input  [1:0] memSel,
  input  RegWrtEn,
  input  isLoad,
  input  isStore,
  input  [3:0] rd,
  input  [31:0] aluOut,
  input  [31:0] DataOut2,
  input  CLK,
  input  RST,
  output [31:0] nxtPC,
  output [1:0] memSelOut,
  output RegWrtEnOut,
  output isLoadOut,
  output isStoreOut,
  output [3:0] rd_2,
  output [31:0] AluOutOut,
  output [31:0] DataOut2Out
);

  Register #(.width(32)) register_1 (.D(PCinc), .Q(nxtPC), .clk(CLK), .clr(RST));  // open: en
  Register #(.width(2)) register_2 (.D(memSel), .Q(memSelOut), .clk(CLK), .clr(RST));  // open: en
  Register #(.width(1)) register_3 (.D(RegWrtEn), .Q(RegWrtEnOut), .clk(CLK), .clr(RST));  // open: en
  Register #(.width(1)) register_4 (.D(isLoad), .Q(isLoadOut), .clk(CLK), .clr(RST));  // open: en
  Register #(.width(1)) register_5 (.D(isStore), .Q(isStoreOut), .clk(CLK), .clr(RST));  // open: en
  Register #(.width(4)) register_6 (.D(rd), .Q(rd_2), .clk(CLK), .clr(RST));  // open: en
  Register #(.width(32)) register_7 (.D(aluOut), .Q(AluOutOut), .clk(CLK), .clr(RST));  // open: en
  Register #(.width(32)) register_8 (.D(DataOut2), .Q(DataOut2Out), .clk(CLK), .clr(RST));  // open: en
endmodule

// RF
module Register_File (
  input  [3:0] RS1,
  input  [3:0] RS2,
  input  EN,
  input  [3:0] RD,
  input  [31:0] DataIn,
  input  CLK,
  input  RST,
  output [31:0] Data1,
  output [31:0] Data2
);

  wire demultiplexer_1_out0, demultiplexer_1_out1, demultiplexer_1_out2, demultiplexer_1_out3,
       demultiplexer_1_out4, demultiplexer_1_out5, demultiplexer_1_out6, demultiplexer_1_out7,
       demultiplexer_1_out8, demultiplexer_1_out9, demultiplexer_1_out10, demultiplexer_1_out11,
       demultiplexer_1_out12, demultiplexer_1_out13, demultiplexer_1_out14, demultiplexer_1_out15;
  wire [31:0] register_1_q, register_2_q, register_3_q, register_4_q, register_5_q, register_6_q,
       register_7_q, register_8_q, register_9_q, register_10_q, register_11_q, register_12_q, register_13_q,
       register_14_q, register_15_q, register_16_q;

  Demultiplexer #(.select(4), .disabled(0), .enable("false")) demultiplexer_1 (
    .out0(demultiplexer_1_out0), .out1(demultiplexer_1_out1), .out2(demultiplexer_1_out2),
    .out3(demultiplexer_1_out3), .out4(demultiplexer_1_out4), .out5(demultiplexer_1_out5),
    .out6(demultiplexer_1_out6), .out7(demultiplexer_1_out7), .out8(demultiplexer_1_out8),
    .out9(demultiplexer_1_out9), .out10(demultiplexer_1_out10), .out11(demultiplexer_1_out11),
    .out12(demultiplexer_1_out12), .out13(demultiplexer_1_out13), .out14(demultiplexer_1_out14),
    .out15(demultiplexer_1_out15), .in(EN), .sel(RD));
  Register #(.width(32)) register_1 (.D(DataIn), .en(demultiplexer_1_out0), .Q(register_1_q), .clk(CLK), .clr(RST));
  Register #(.width(32)) register_2 (.D(DataIn), .en(demultiplexer_1_out1), .Q(register_2_q), .clk(CLK), .clr(RST));
  Register #(.width(32)) register_3 (.D(DataIn), .en(demultiplexer_1_out2), .Q(register_3_q), .clk(CLK), .clr(RST));
  Register #(.width(32)) register_4 (.D(DataIn), .en(demultiplexer_1_out3), .Q(register_4_q), .clk(CLK), .clr(RST));
  Register #(.width(32)) register_5 (.D(DataIn), .en(demultiplexer_1_out4), .Q(register_5_q), .clk(CLK), .clr(RST));
  Register #(.width(32)) register_6 (.D(DataIn), .en(demultiplexer_1_out5), .Q(register_6_q), .clk(CLK), .clr(RST));
  Register #(.width(32)) register_7 (.D(DataIn), .en(demultiplexer_1_out6), .Q(register_7_q), .clk(CLK), .clr(RST));
  Register #(.width(32)) register_8 (.D(DataIn), .en(demultiplexer_1_out7), .Q(register_8_q), .clk(CLK), .clr(RST));
  Register #(.width(32)) register_9 (.D(DataIn), .en(demultiplexer_1_out8), .Q(register_9_q), .clk(CLK), .clr(RST));
  Register #(.width(32)) register_10 (.D(DataIn), .en(demultiplexer_1_out9), .Q(register_10_q), .clk(CLK), .clr(RST));
  Register #(.width(32)) register_11 (.D(DataIn), .en(demultiplexer_1_out10), .Q(register_11_q), .clk(CLK), .clr(RST));
  Register #(.width(32)) register_12 (.D(DataIn), .en(demultiplexer_1_out11), .Q(register_12_q), .clk(CLK), .clr(RST));
  Register #(.width(32)) register_13 (.D(DataIn), .en(demultiplexer_1_out12), .Q(register_13_q), .clk(CLK), .clr(RST));
  Register #(.width(32)) register_14 (.D(DataIn), .en(demultiplexer_1_out13), .Q(register_14_q), .clk(CLK), .clr(RST));
  Register #(.width(32)) register_15 (.D(DataIn), .en(demultiplexer_1_out14), .Q(register_15_q), .clk(CLK), .clr(RST));
  Register #(.width(32)) register_16 (.D(DataIn), .en(demultiplexer_1_out15), .Q(register_16_q), .clk(CLK), .clr(RST));
  Multiplexer #(.select(4), .width(32), .enable("false")) multiplexer_1 (
    .in0(register_1_q), .in1(register_2_q), .in2(register_3_q), .in3(register_4_q), .in4(register_5_q),
    .in5(register_6_q), .in6(register_7_q), .in7(register_8_q), .in8(register_9_q), .in9(register_10_q),
    .in10(register_11_q), .in11(register_12_q), .in12(register_13_q), .in13(register_14_q),
    .in14(register_15_q), .in15(register_16_q), .out(Data1), .sel(RS1));
  Multiplexer #(.select(4), .width(32), .enable("false")) multiplexer_2 (
    .in0(register_1_q), .in1(register_2_q), .in2(register_3_q), .in3(register_4_q), .in4(register_5_q),
    .in5(register_6_q), .in6(register_7_q), .in7(register_8_q), .in8(register_9_q), .in9(register_10_q),
    .in10(register_11_q), .in11(register_12_q), .in12(register_13_q), .in13(register_14_q),
    .in14(register_15_q), .in15(register_16_q), .out(Data2), .sel(RS2));
endmodule

module ALU (
  input  [31:0] in_1,
  input  [31:0] in_2,
  input  [4:0] in_3,
  output [31:0] DataOut,
  output cmpOut
);

  wire comparator_1_eq, comparator_1_gt, comparator_1_lt, comparator_2_eq, comparator_2_gt, comparator_2_lt,
       multiplexer_2_out, not_1_out, not_2_out, or_2_out, or_3_out, or_4_out, or_5_out;
  wire [31:0] adder_1_out, and_1_out, bit_extender_1_out, multiplexer_1_out, nand_1_out, nor_1_out, or_1_out,
       subtractor_1_out, xnor_1_out, xor_1_out;

  Adder #(.width(32)) adder_1 (.a(in_1), .b(in_2), .out(adder_1_out));  // open: cin, cout
  Subtractor #(.width(32)) subtractor_1 (.a(in_1), .b(in_2), .out(subtractor_1_out));  // open: bin, bout
  assign and_1_out = in_1 & in_2;  // AND_Gate and_1, 32 bits wide
  assign or_1_out = in_1 | in_2;  // OR_Gate or_1, 32 bits wide
  assign xor_1_out = in_1 ^ in_2;  // XOR_Gate xor_1, 32 bits wide
  assign nand_1_out = ~(in_1 & in_2);  // NAND_Gate nand_1, 32 bits wide
  assign nor_1_out = ~(in_1 | in_2);  // NOR_Gate nor_1, 32 bits wide
  Comparator #(.width(32)) comparator_1 (
    .a(in_1), .b({32{1'b0}}), .gt(comparator_1_gt), .eq(comparator_1_eq), .lt(comparator_1_lt));
  assign xnor_1_out = ~(in_1 ^ in_2);  // XNOR_Gate xnor_1, 32 bits wide
  Comparator #(.width(32)) comparator_2 (
    .a(in_1), .b(in_2), .gt(comparator_2_gt), .eq(comparator_2_eq), .lt(comparator_2_lt));
  or or_2 (or_2_out, comparator_1_lt, comparator_1_eq);
  not not_1 (not_1_out, comparator_1_eq);
  or or_3 (or_3_out, comparator_1_gt, comparator_1_eq);
  or or_4 (or_4_out, comparator_2_lt, comparator_2_eq);
  not not_2 (not_2_out, comparator_2_eq);
  or or_5 (or_5_out, comparator_2_gt, comparator_2_eq);
  Multiplexer #(.select(4), .width(32), .enable("false")) multiplexer_1 (
    .in0(adder_1_out), .in1(subtractor_1_out), .in2({32{1'b0}}), .in3({32{1'b0}}), .in4(and_1_out),
    .in5(or_1_out), .in6(xor_1_out), .in7({32{1'b0}}), .in8({32{1'b0}}), .in9({32{1'b0}}), .in10({32{1'b0}}),
    .in11({in_2[15:0], {16{1'b0}}}), .in12(nand_1_out), .in13(nor_1_out), .in14(xnor_1_out),
    .in15({32{1'b0}}), .out(multiplexer_1_out), .sel(in_3[3:0]));
  Multiplexer #(.select(4), .enable("false")) multiplexer_2 (
    .in0(1'b0), .in1(comparator_2_eq), .in2(comparator_2_lt), .in3(or_4_out), .in4(1'b0),
    .in5(comparator_1_eq), .in6(comparator_1_lt), .in7(or_2_out), .in8(1'b1), .in9(not_2_out),
    .in10(or_5_out), .in11(comparator_2_gt), .in12(1'b0), .in13(not_1_out), .in14(or_3_out),
    .in15(comparator_1_gt), .out(multiplexer_2_out), .sel(in_3[3:0]));
  Multiplexer #(.width(32), .disabled(0), .enable("false")) multiplexer_3 (
    .in0(multiplexer_1_out), .in1(bit_extender_1_out), .out(DataOut), .sel(in_3[4]));
  Multiplexer #(.disabled(0), .enable("false")) multiplexer_4 (
    .in0(1'b0), .in1(multiplexer_2_out), .out(cmpOut), .sel(in_3[4]));
  assign bit_extender_1_out = {{31{1'b0}}, cmpOut};  // Bit_Extender bit_extender_1

  // Other names for the same wires on the sheet: Sel[3:0] = in_3[3:0]; Cmp = in_3[4]
endmodule

// Control
module Controller (
  input  ALUcmpIn,
  input  [31:0] iWord,
  input  bubble,
  output [1:0] memOutSel,
  output RegWrtEn,
  output isLoad,
  output isStore,
  output [1:0] pcSel,
  output immsel,
  output [3:0] RD,
  output [3:0] RS2,
  output [3:0] RS1,
  output [4:0] sndOp,
  output [31:0] SeImm
);

  wire cmpsel, comparator_1_eq, comparator_2_eq, comparator_4_eq, isLoad_t, isStore_t, or_2_out, RegWrtEn_t,
       weird;
  wire [1:0] pcsel_t;
  wire [15:0] multiplexer_5_out;
  wire [31:0] shifter_1_out, sxt_1_out_2;

  Multiplexer #(.select(4), .width(8), .enable("false")) multiplexer_1 (
    .in0(8'h80), .in1({8{1'b0}}), .in2(8'h80), .in3({8{1'b0}}), .in4({8{1'b0}}), .in5(8'h41),
    .in6({{5{1'b0}}, ALUcmpIn, 2'b00}), .in7({8{1'b0}}), .in8(8'hc0), .in9(8'hd2), .in10(8'hc0),
    .in11(8'he8), .in12({8{1'b0}}), .in13({8{1'b0}}), .in14({8{1'b0}}), .in15({8{1'b0}}),
    .out({RegWrtEn_t, immsel, memOutSel, pcsel_t, isLoad_t, isStore_t}), .sel(iWord[31:28]));
  Comparator #(.width(4)) comparator_1 (.a(4'b0101), .b(iWord[31:28]), .eq(comparator_1_eq));  // open: gt, lt
  Comparator #(.width(4)) comparator_2 (.a(iWord[31:28]), .b(4'b0110), .eq(comparator_2_eq));  // open: gt, lt
  Comparator #(.width(2)) comparator_3 (.a(iWord[29:28]), .b(2'b10), .eq(cmpsel));  // open: gt, lt
  or or_1 (weird, comparator_1_eq, comparator_2_eq);
  Multiplexer #(.width(4), .enable("false")) multiplexer_2 (.in0(iWord[23:20]), .in1(4'b0000), .out(RD), .sel(weird));
  Multiplexer #(.width(4), .enable("false")) multiplexer_3 (
    .in0(iWord[19:16]), .in1(iWord[23:20]), .out(RS1), .sel(weird));
  Multiplexer #(.select(2), .width(4), .enable("false")) multiplexer_4 (
    .in0(iWord[15:12]), .in1(iWord[19:16]), .in2(4'b0000), .in3(4'b0000), .out(RS2), .sel({iWord[31], weird}));
  Multiplexer #(.width(16), .enable("false")) multiplexer_5 (
    .in0({16{1'b0}}), .in1(iWord[15:0]), .out(multiplexer_5_out), .sel(or_2_out));
  or or_2 (or_2_out, iWord[31], weird);
  sxt sxt_1 (.in_1(multiplexer_5_out), .out_2(sxt_1_out_2));
  Shifter #(.width(32)) shifter_1 (.in(sxt_1_out_2), .\dist (5'b00010), .out(shifter_1_out));
  Multiplexer #(.enable("false")) multiplexer_6 (.in0(1'b0), .in1(1'b1), .out(sndOp[4]), .sel(cmpsel));
  Multiplexer #(.width(4), .enable("false")) multiplexer_7 (
    .in0(iWord[27:24]), .in1(4'b0000), .out(sndOp[3:0]), .sel(iWord[28]));
  Multiplexer #(.width(3), .enable("false")) multiplexer_8 (
    .in0({isStore_t, isLoad_t, RegWrtEn_t}), .in1(3'b000), .out({isStore, isLoad, RegWrtEn}), .sel(bubble));
  Multiplexer #(.width(2), .enable("false")) multiplexer_9 (.in0(pcsel_t), .in1(2'b11), .out(pcSel), .sel(bubble));
  Multiplexer #(.width(32), .enable("false")) multiplexer_10 (
    .in0(sxt_1_out_2), .in1(shifter_1_out), .out(SeImm), .sel(comparator_4_eq));
  Comparator #(.width(4)) comparator_4 (.a(4'b1011), .b(iWord[31:28]), .eq(comparator_4_eq));  // open: gt, lt

  // Other names for the same wires on the sheet: memsel[1:0] = memOutSel; bit3 = iWord[31];
  //   Family[3:0] = iWord[31:28]; imm[15:0] = iWord[15:0]; _1512[3:0] = iWord[15:12]; _1916[3:0] = iWord[19:16];
  //   _2320[3:0] = iWord[23:20]; sndop_t[3:0] = iWord[27:24]; sndopsel = iWord[28]
endmodule

// SXT
module sxt (
  input  [15:0] in_1,
  output [31:0] out_2
);


  assign out_2 = {{17{in_1[15]}}, in_1[14:0]};
endmodule

// DM
module DataMemory (
  input  [31:0] ADDR,
  input  [31:0] Din,
  input  str,
  input  ld,
  input  [9:0] Sw,
  input  [3:0] Key,
  input  CLK,
  input  RST,
  output [31:0] Dout,
  output [15:0] HEX,
  output [9:0] LEDR,
  output [7:0] LEDG
);

  wire comparator_1_eq, comparator_1_gt, or_1_out;
  wire [31:0] iocontrol_1_dbus_2, n32bmem_1_dout;

  _32BMem u_32bmem_1 (.ADDR(ADDR), .Din(Din), .str(str), .CLK(CLK), .RST(RST), .Dout(n32bmem_1_dout));
  IoControl iocontrol_1 (
    .ABus(ADDR), .DBus(Din), .WE(str), .SW(Sw), .KEYS(Key), .RST(RST), .DBus_2(iocontrol_1_dbus_2),
    .LEDG(LEDG), .LEDR(LEDR), .HEX(HEX));
  Comparator #(.width(32), .mode("unsigned")) comparator_1 (
    .a(ADDR), .b(32'hf0000000), .gt(comparator_1_gt), .eq(comparator_1_eq));  // open: lt
  or or_1 (or_1_out, comparator_1_gt, comparator_1_eq);
  Multiplexer #(.width(32), .enable("false")) multiplexer_1 (
    .in0(n32bmem_1_dout), .in1(iocontrol_1_dbus_2), .out(Dout), .sel(or_1_out));
endmodule

module _26bMem (
  input  [25:0] ADDR,
  input  RST,
  input  [31:0] Data,
  input  CLK,
  input  ld,
  output [31:0] Dout
);

  wire demultiplexer_1_out0, demultiplexer_1_out1, demultiplexer_1_out2, demultiplexer_1_out3;
  wire [31:0] ram_1_data, ram_2_data, ram_3_data, ram_4_data;

  Demultiplexer #(.select(2), .enable("false")) demultiplexer_1 (
    .out0(demultiplexer_1_out0), .out1(demultiplexer_1_out1), .out2(demultiplexer_1_out2),
    .out3(demultiplexer_1_out3), .in(ld), .sel(ADDR[25:24]));
  RAM #(.addrWidth(24), .dataWidth(32), .bus("separate")) ram_1 (
    .addr(ADDR[23:0]), .din(Data), .data(ram_1_data), .str(demultiplexer_1_out0), .clk(CLK), .ld(1'b1),
    .clr(RST));  // open: sel
  RAM #(.addrWidth(24), .dataWidth(32), .bus("separate")) ram_2 (
    .addr(ADDR[23:0]), .din(Data), .data(ram_2_data), .str(demultiplexer_1_out1), .clk(CLK), .ld(1'b1),
    .clr(RST));  // open: sel
  RAM #(.addrWidth(24), .dataWidth(32), .bus("separate")) ram_3 (
    .addr(ADDR[23:0]), .din(Data), .data(ram_3_data), .str(demultiplexer_1_out2), .clk(CLK), .ld(1'b1),
    .clr(RST));  // open: sel
  RAM #(.addrWidth(24), .dataWidth(32), .bus("separate")) ram_4 (
    .addr(ADDR[23:0]), .din(Data), .data(ram_4_data), .str(demultiplexer_1_out3), .clk(CLK), .ld(1'b1),
    .clr(RST));  // open: sel
  Multiplexer #(.select(2), .width(32), .enable("false")) multiplexer_1 (
    .in0(ram_1_data), .in1(ram_2_data), .in2(ram_3_data), .in3(ram_4_data), .out(Dout), .sel(ADDR[25:24]));

  // Other names for the same wires on the sheet: LoAddr[23:0] = ADDR[23:0]; memSel[1:0] = ADDR[25:24];
  //   Din[31:0] = Data; str = ld
endmodule

module _28bMem (
  input  [27:0] ADDR,
  input  RST,
  input  [31:0] Din,
  input  CLK,
  input  str,
  output [31:0] Dout
);

  wire demultiplexer_1_out0, demultiplexer_1_out1, demultiplexer_1_out2, demultiplexer_1_out3;
  wire [31:0] n26bmem_1_dout, n26bmem_2_dout, n26bmem_3_dout, n26bmem_4_dout;

  Demultiplexer #(.select(2), .enable("false")) demultiplexer_1 (
    .out0(demultiplexer_1_out0), .out1(demultiplexer_1_out1), .out2(demultiplexer_1_out2),
    .out3(demultiplexer_1_out3), .in(str), .sel(ADDR[27:26]));
  _26bMem u_26bmem_1 (
    .ADDR(ADDR[25:0]), .Data(Din), .ld(demultiplexer_1_out0), .CLK(CLK), .RST(RST), .Dout(n26bmem_1_dout));
  _26bMem u_26bmem_2 (
    .ADDR(ADDR[25:0]), .Data(Din), .ld(demultiplexer_1_out1), .CLK(CLK), .RST(RST), .Dout(n26bmem_2_dout));
  _26bMem u_26bmem_3 (
    .ADDR(ADDR[25:0]), .Data(Din), .ld(demultiplexer_1_out2), .CLK(CLK), .RST(RST), .Dout(n26bmem_3_dout));
  _26bMem u_26bmem_4 (
    .ADDR(ADDR[25:0]), .Data(Din), .ld(demultiplexer_1_out3), .CLK(CLK), .RST(RST), .Dout(n26bmem_4_dout));
  Multiplexer #(.select(2), .width(32), .enable("false")) multiplexer_1 (
    .in0(n26bmem_1_dout), .in1(n26bmem_2_dout), .in2(n26bmem_3_dout), .in3(n26bmem_4_dout), .out(Dout),
    .sel(ADDR[27:26]));

  // Other names for the same wires on the sheet: LoAddr[25:0] = ADDR[25:0]; memSel[1:0] = ADDR[27:26];
  //   Data[31:0] = Din
endmodule

module _30bMem (
  input  [29:0] ADDR,
  input  RST,
  input  [31:0] Din,
  input  CLK,
  input  str,
  output [31:0] Dout
);

  wire demultiplexer_1_out0, demultiplexer_1_out1, demultiplexer_1_out2, demultiplexer_1_out3;
  wire [31:0] n28bmem_1_dout, n28bmem_2_dout, n28bmem_3_dout, n28bmem_4_dout;

  Demultiplexer #(.select(2), .enable("false")) demultiplexer_1 (
    .out0(demultiplexer_1_out0), .out1(demultiplexer_1_out1), .out2(demultiplexer_1_out2),
    .out3(demultiplexer_1_out3), .in(str), .sel(ADDR[29:28]));
  _28bMem u_28bmem_1 (
    .ADDR(ADDR[27:0]), .Din(Din), .str(demultiplexer_1_out0), .CLK(CLK), .RST(RST), .Dout(n28bmem_1_dout));
  _28bMem u_28bmem_2 (
    .ADDR(ADDR[27:0]), .Din(Din), .str(demultiplexer_1_out1), .CLK(CLK), .RST(RST), .Dout(n28bmem_2_dout));
  _28bMem u_28bmem_3 (
    .ADDR(ADDR[27:0]), .Din(Din), .str(demultiplexer_1_out2), .CLK(CLK), .RST(RST), .Dout(n28bmem_3_dout));
  _28bMem u_28bmem_4 (
    .ADDR(ADDR[27:0]), .Din(Din), .str(demultiplexer_1_out3), .CLK(CLK), .RST(RST), .Dout(n28bmem_4_dout));
  Multiplexer #(.select(2), .width(32), .enable("false")) multiplexer_1 (
    .in0(n28bmem_1_dout), .in1(n28bmem_2_dout), .in2(n28bmem_3_dout), .in3(n28bmem_4_dout), .out(Dout),
    .sel(ADDR[29:28]));

  // Other names for the same wires on the sheet: LoAddr[27:0] = ADDR[27:0]; memSel[1:0] = ADDR[29:28];
  //   Data[31:0] = Din
endmodule

module BranchAddrCalculator (
  input  [31:0] nxtPC,
  input  [31:0] seImm,
  output [31:0] brAddr
);

  wire [31:0] shifter_1_out;

  Shifter #(.width(32)) shifter_1 (.in(seImm), .\dist (5'b00010), .out(shifter_1_out));
  Adder #(.width(32)) adder_1 (.a(nxtPC), .b(shifter_1_out), .out(brAddr));  // open: cin, cout
endmodule

module PC (
  input  [31:0] in_1,
  input  CLK,
  input  RST,
  output [31:0] out_4
);

  wire register_2_q;
  wire [31:0] register_1_q;

  Register #(.width(32)) register_1 (.D(in_1), .Q(register_1_q), .clk(CLK), .clr(RST));  // open: en
  Register #(.width(1)) register_2 (.D(RST), .Q(register_2_q), .clk(RST), .clr(CLK));  // open: en
  Multiplexer #(.width(32), .enable("false")) multiplexer_1 (
    .in0(register_1_q), .in1(32'h40), .out(out_4), .sel(register_2_q));
endmodule

// pcsel
module pcSel (
  input  JAL,
  input  branch,
  input  bubble,
  output [1:0] out_4
);

  or or_1 (out_4[1], JAL, branch);
  Multiplexer #(.enable("false")) multiplexer_1 (.in0(bubble), .in1(JAL), .out(out_4[0]), .sel(out_4[1]));

  // Other names for the same wires on the sheet: bit1 = out_4[1]
endmodule

module IR (
  input  [10:0] pcIn,
  output [31:0] dOut
);

  wire [10:0] adder_1_out, adder_2_out, adder_3_out;

  Adder #(.width(11)) adder_1 (.a(pcIn), .b(11'h1), .out(adder_1_out));  // open: cin, cout
  Adder #(.width(11)) adder_2 (.a(adder_1_out), .b(11'h1), .out(adder_2_out));  // open: cin, cout
  Adder #(.width(11)) adder_3 (.a(adder_2_out), .b(11'h1), .out(adder_3_out));  // open: cin, cout
  ROM #(.addrWidth(11)) rom_1 (.addr(pcIn), .data(dOut[31:24]));  // open: sel
  ROM #(.addrWidth(11)) rom_2 (.addr(adder_1_out), .data(dOut[23:16]));  // open: sel
  ROM #(.addrWidth(11)) rom_3 (.addr(adder_2_out), .data(dOut[15:8]));  // open: sel
  ROM #(.addrWidth(11)) rom_4 (.addr(adder_3_out), .data(dOut[7:0]));  // open: sel

  // Notes on the sheet:
  //   contents of rom_1 (hex, n*v repeats v):
  //   68 44 0 8 80 77 0 1 80 77 0 1 80 77 0 1 80 77 0 1 80 77 0 1 80 77 0 1 80 77 0 1 80 77 0 1 8b c0 f0 0
  //   84 66 0 0 c 46 60 0 50 c4 0 4 80 46 b ad 50 c4 0 0 68 44 ff f9 80 86 b ef 6 dd d0 0 8b c0 f0 0 8b 60
  //   0 0 80 66 0 1 50 c6 0 8 50 cd 0 4 80 66 0 1 50 c6 0 8 80 4d ff ff 80 5d 0 2 80 d 0 1 0 14 50 0 61 1
  //   0 4 c 4d d0 0 50 c4 0 4 50 c0 0 0 68 44 ff fc 80 66 0 1 50 c6 0 8 80 4d 0 7 80 54 0 3 0 5 50 0 85 10
  //   0 25 84 21 0 d1 6 0 10 0 5 10 40 0 d 24 20 0 c 32 10 0 1 14 20 0 4 41 20 0 e 11 40 0 6 22 30 0 1 0
  //   20 0 0 1 0 0 80 5d ff f8 69 5 0 4 c 4d d0 0 50 c4 0 4 50 c0 0 0 68 44 ff fc 80 66 0 1 50 c6 0 8 80
  //   1d 0 1 80 4d 0 4b 80 5d 0 22 80 d ff b0 23 24 50 0 69 2d 0 45 80 66 0 1 50 c6 0 8 22 24 50 0 69 2d 0
  //   41 80 66 0 1 50 c6 0 8 21 24 50 0 69 2d 0 3d 80 66 0 1 50 c6 0 8 29 24 50 0 69 21 0 39 80 66 0 1 50
  //   c6 0 8 2b 24 50 0 69 21 0 35 80 66 0 1 50 c6 0 8 2a 24 50 0 69 21 0 31 80 66 0 1 50 c6 0 8 23 25 50
  //   0 69 21 0 2d 80 66 0 1 50 c6 0 8 22 25 50 0 69 2d 0 29 80 66 0 1 50 c6 0 8 21 25 50 0 69 21 0 25 80
  //   66 0 1 50 c6 0 8 29 25 50 0 69 2d 0 21 80 66 0 1 50 c6 0 8 2b 25 50 0 69 2d 0 1d 80 66 0 1 50 c6 0 8
  //   2a 25 50 0 69 21 0 19 80 66 0 1 50 c6 0 8 23 20 40 0 69 21 0 15 80 66 0 1 50 c6 0 8 22 20 40 0 69 21
  //   0 11 80 66 0 1 50 c6 0 8 21 20 40 0 69 2d 0 d 80 66 0 1 50 c6 0 8 29 20 40 0 69 21 0 9 80 66 0 1 50
  //   c6 0 8 2b 20 40 0 69 2d 0 5 80 66 0 1 50 c6 0 8 2a 20 40 0 69 2d 0 1 68 44 0 4 c 4c c0 0 50 c4 0 4
  //   50 c2 0 0 68 44 ff fc 80 66 0 1 50 c6 0 8 80 4d 0 37 80 5d 0 e1 80 2d 4 0 50 24 0 0 50 25 0 4 80 22
  //   0 4 90 2 0 0 69 5 0 2 90 2 ff fc 61 4 0 4 c 4d d0 0 50 c4 0 4 50 c0 0 0 68 44 ff fc 80 66 0 1 50 c6
  //   0 8 80 5d 2 78 b0 4d 0 9f 68 44 0 6 69 45 0 1 b0 54 0 0 c 4d d0 0 50 c4 0 4 50 c4 0 0 68 44 ff fc 80
  //   66 0 1 50 c6 0 8 90 5c 0 10 50 c5 0 0 61 5d ff fd 90 5c 0 10 50 c5 0 0 69 5d ff fd c 4d d0 0 50 c4 0
  //   8 50 c4 0 0 68 44 ff fc
  //   contents of rom_2 (hex, n*v repeats v):
  //   68 44 0 8 80 77 0 1 80 77 0 1 80 77 0 1 80 77 0 1 80 77 0 1 80 77 0 1 80 77 0 1 80 77 0 1 8b c0 f0 0
  //   84 66 0 0 c 46 60 0 50 c4 0 4 80 46 b ad 50 c4 0 0 68 44 ff f9 80 86 b ef 6 dd d0 0 8b c0 f0 0 8b 60
  //   0 0 80 66 0 1 50 c6 0 8 50 cd 0 4 80 66 0 1 50 c6 0 8 80 4d ff ff 80 5d 0 2 80 d 0 1 0 14 50 0 61 1
  //   0 4 c 4d d0 0 50 c4 0 4 50 c0 0 0 68 44 ff fc 80 66 0 1 50 c6 0 8 80 4d 0 7 80 54 0 3 0 5 50 0 85 10
  //   0 25 84 21 0 d1 6 0 10 0 5 10 40 0 d 24 20 0 c 32 10 0 1 14 20 0 4 41 20 0 e 11 40 0 6 22 30 0 1 0
  //   20 0 0 1 0 0 80 5d ff f8 69 5 0 4 c 4d d0 0 50 c4 0 4 50 c0 0 0 68 44 ff fc 80 66 0 1 50 c6 0 8 80
  //   1d 0 1 80 4d 0 4b 80 5d 0 22 80 d ff b0 23 24 50 0 69 2d 0 45 80 66 0 1 50 c6 0 8 22 24 50 0 69 2d 0
  //   41 80 66 0 1 50 c6 0 8 21 24 50 0 69 2d 0 3d 80 66 0 1 50 c6 0 8 29 24 50 0 69 21 0 39 80 66 0 1 50
  //   c6 0 8 2b 24 50 0 69 21 0 35 80 66 0 1 50 c6 0 8 2a 24 50 0 69 21 0 31 80 66 0 1 50 c6 0 8 23 25 50
  //   0 69 21 0 2d 80 66 0 1 50 c6 0 8 22 25 50 0 69 2d 0 29 80 66 0 1 50 c6 0 8 21 25 50 0 69 21 0 25 80
  //   66 0 1 50 c6 0 8 29 25 50 0 69 2d 0 21 80 66 0 1 50 c6 0 8 2b 25 50 0 69 2d 0 1d 80 66 0 1 50 c6 0 8
  //   2a 25 50 0 69 21 0 19 80 66 0 1 50 c6 0 8 23 20 40 0 69 21 0 15 80 66 0 1 50 c6 0 8 22 20 40 0 69 21
  //   0 11 80 66 0 1 50 c6 0 8 21 20 40 0 69 2d 0 d 80 66 0 1 50 c6 0 8 29 20 40 0 69 21 0 9 80 66 0 1 50
  //   c6 0 8 2b 20 40 0 69 2d 0 5 80 66 0 1 50 c6 0 8 2a 20 40 0 69 2d 0 1 68 44 0 4 c 4c c0 0 50 c4 0 4
  //   50 c2 0 0 68 44 ff fc 80 66 0 1 50 c6 0 8 80 4d 0 37 80 5d 0 e1 80 2d 4 0 50 24 0 0 50 25 0 4 80 22
  //   0 4 90 2 0 0 69 5 0 2 90 2 ff fc 61 4 0 4 c 4d d0 0 50 c4 0 4 50 c0 0 0 68 44 ff fc 80 66 0 1 50 c6
  //   0 8 80 5d 2 78 b0 4d 0 9f 68 44 0 6 69 45 0 1 b0 54 0 0 c 4d d0 0 50 c4 0 4 50 c4 0 0 68 44 ff fc 80
  //   66 0 1 50 c6 0 8 90 5c 0 10 50 c5 0 0 61 5d ff fd 90 5c 0 10 50 c5 0 0 69 5d ff fd c 4d d0 0 50 c4 0
  //   8 50 c4 0 0 68 44 ff fc
  //   contents of rom_3 (hex, n*v repeats v):
  //   68 44 0 8 80 77 0 1 80 77 0 1 80 77 0 1 80 77 0 1 80 77 0 1 80 77 0 1 80 77 0 1 80 77 0 1 8b c0 f0 0
  //   84 66 0 0 c 46 60 0 50 c4 0 4 80 46 b ad 50 c4 0 0 68 44 ff f9 80 86 b ef 6 dd d0 0 8b c0 f0 0 8b 60
  //   0 0 80 66 0 1 50 c6 0 8 50 cd 0 4 80 66 0 1 50 c6 0 8 80 4d ff ff 80 5d 0 2 80 d 0 1 0 14 50 0 61 1
  //   0 4 c 4d d0 0 50 c4 0 4 50 c0 0 0 68 44 ff fc 80 66 0 1 50 c6 0 8 80 4d 0 7 80 54 0 3 0 5 50 0 85 10
  //   0 25 84 21 0 d1 6 0 10 0 5 10 40 0 d 24 20 0 c 32 10 0 1 14 20 0 4 41 20 0 e 11 40 0 6 22 30 0 1 0
  //   20 0 0 1 0 0 80 5d ff f8 69 5 0 4 c 4d d0 0 50 c4 0 4 50 c0 0 0 68 44 ff fc 80 66 0 1 50 c6 0 8 80
  //   1d 0 1 80 4d 0 4b 80 5d 0 22 80 d ff b0 23 24 50 0 69 2d 0 45 80 66 0 1 50 c6 0 8 22 24 50 0 69 2d 0
  //   41 80 66 0 1 50 c6 0 8 21 24 50 0 69 2d 0 3d 80 66 0 1 50 c6 0 8 29 24 50 0 69 21 0 39 80 66 0 1 50
  //   c6 0 8 2b 24 50 0 69 21 0 35 80 66 0 1 50 c6 0 8 2a 24 50 0 69 21 0 31 80 66 0 1 50 c6 0 8 23 25 50
  //   0 69 21 0 2d 80 66 0 1 50 c6 0 8 22 25 50 0 69 2d 0 29 80 66 0 1 50 c6 0 8 21 25 50 0 69 21 0 25 80
  //   66 0 1 50 c6 0 8 29 25 50 0 69 2d 0 21 80 66 0 1 50 c6 0 8 2b 25 50 0 69 2d 0 1d 80 66 0 1 50 c6 0 8
  //   2a 25 50 0 69 21 0 19 80 66 0 1 50 c6 0 8 23 20 40 0 69 21 0 15 80 66 0 1 50 c6 0 8 22 20 40 0 69 21
  //   0 11 80 66 0 1 50 c6 0 8 21 20 40 0 69 2d 0 d 80 66 0 1 50 c6 0 8 29 20 40 0 69 21 0 9 80 66 0 1 50
  //   c6 0 8 2b 20 40 0 69 2d 0 5 80 66 0 1 50 c6 0 8 2a 20 40 0 69 2d 0 1 68 44 0 4 c 4c c0 0 50 c4 0 4
  //   50 c2 0 0 68 44 ff fc 80 66 0 1 50 c6 0 8 80 4d 0 37 80 5d 0 e1 80 2d 4 0 50 24 0 0 50 25 0 4 80 22
  //   0 4 90 2 0 0 69 5 0 2 90 2 ff fc 61 4 0 4 c 4d d0 0 50 c4 0 4 50 c0 0 0 68 44 ff fc 80 66 0 1 50 c6
  //   0 8 80 5d 2 78 b0 4d 0 9f 68 44 0 6 69 45 0 1 b0 54 0 0 c 4d d0 0 50 c4 0 4 50 c4 0 0 68 44 ff fc 80
  //   66 0 1 50 c6 0 8 90 5c 0 10 50 c5 0 0 61 5d ff fd 90 5c 0 10 50 c5 0 0 69 5d ff fd c 4d d0 0 50 c4 0
  //   8 50 c4 0 0 68 44 ff fc
  //   contents of rom_4 (hex, n*v repeats v):
  //   68 44 0 8 80 77 0 1 80 77 0 1 80 77 0 1 80 77 0 1 80 77 0 1 80 77 0 1 80 77 0 1 80 77 0 1 8b c0 f0 0
  //   84 66 0 0 c 46 60 0 50 c4 0 4 80 46 b ad 50 c4 0 0 68 44 ff f9 80 86 b ef 6 dd d0 0 8b c0 f0 0 8b 60
  //   0 0 80 66 0 1 50 c6 0 8 50 cd 0 4 80 66 0 1 50 c6 0 8 80 4d ff ff 80 5d 0 2 80 d 0 1 0 14 50 0 61 1
  //   0 4 c 4d d0 0 50 c4 0 4 50 c0 0 0 68 44 ff fc 80 66 0 1 50 c6 0 8 80 4d 0 7 80 54 0 3 0 5 50 0 85 10
  //   0 25 84 21 0 d1 6 0 10 0 5 10 40 0 d 24 20 0 c 32 10 0 1 14 20 0 4 41 20 0 e 11 40 0 6 22 30 0 1 0
  //   20 0 0 1 0 0 80 5d ff f8 69 5 0 4 c 4d d0 0 50 c4 0 4 50 c0 0 0 68 44 ff fc 80 66 0 1 50 c6 0 8 80
  //   1d 0 1 80 4d 0 4b 80 5d 0 22 80 d ff b0 23 24 50 0 69 2d 0 45 80 66 0 1 50 c6 0 8 22 24 50 0 69 2d 0
  //   41 80 66 0 1 50 c6 0 8 21 24 50 0 69 2d 0 3d 80 66 0 1 50 c6 0 8 29 24 50 0 69 21 0 39 80 66 0 1 50
  //   c6 0 8 2b 24 50 0 69 21 0 35 80 66 0 1 50 c6 0 8 2a 24 50 0 69 21 0 31 80 66 0 1 50 c6 0 8 23 25 50
  //   0 69 21 0 2d 80 66 0 1 50 c6 0 8 22 25 50 0 69 2d 0 29 80 66 0 1 50 c6 0 8 21 25 50 0 69 21 0 25 80
  //   66 0 1 50 c6 0 8 29 25 50 0 69 2d 0 21 80 66 0 1 50 c6 0 8 2b 25 50 0 69 2d 0 1d 80 66 0 1 50 c6 0 8
  //   2a 25 50 0 69 21 0 19 80 66 0 1 50 c6 0 8 23 20 40 0 69 21 0 15 80 66 0 1 50 c6 0 8 22 20 40 0 69 21
  //   0 11 80 66 0 1 50 c6 0 8 21 20 40 0 69 2d 0 d 80 66 0 1 50 c6 0 8 29 20 40 0 69 21 0 9 80 66 0 1 50
  //   c6 0 8 2b 20 40 0 69 2d 0 5 80 66 0 1 50 c6 0 8 2a 20 40 0 69 2d 0 1 68 44 0 4 c 4c c0 0 50 c4 0 4
  //   50 c2 0 0 68 44 ff fc 80 66 0 1 50 c6 0 8 80 4d 0 37 80 5d 0 e1 80 2d 4 0 50 24 0 0 50 25 0 4 80 22
  //   0 4 90 2 0 0 69 5 0 2 90 2 ff fc 61 4 0 4 c 4d d0 0 50 c4 0 4 50 c0 0 0 68 44 ff fc 80 66 0 1 50 c6
  //   0 8 80 5d 2 78 b0 4d 0 9f 68 44 0 6 69 45 0 1 b0 54 0 0 c 4d d0 0 50 c4 0 4 50 c4 0 0 68 44 ff fc 80
  //   66 0 1 50 c6 0 8 90 5c 0 10 50 c5 0 0 61 5d ff fd 90 5c 0 10 50 c5 0 0 69 5d ff fd c 4d d0 0 50 c4 0
  //   8 50 c4 0 0 68 44 ff fc
endmodule

module _32BMem (
  input  [31:0] ADDR,
  input  [31:0] Din,
  input  str,
  input  RST,
  input  CLK,
  output [31:0] Dout
);

  wire demultiplexer_1_out0, demultiplexer_1_out1, demultiplexer_1_out2, demultiplexer_1_out3;
  wire [31:0] n30bmem_1_dout, n30bmem_2_dout, n30bmem_3_dout, n30bmem_4_dout;

  Demultiplexer #(.select(2), .enable("false")) demultiplexer_1 (
    .out0(demultiplexer_1_out0), .out1(demultiplexer_1_out1), .out2(demultiplexer_1_out2),
    .out3(demultiplexer_1_out3), .in(str), .sel(ADDR[31:30]));
  _30bMem u_30bmem_1 (
    .ADDR(ADDR[29:0]), .Din(Din), .str(demultiplexer_1_out0), .CLK(CLK), .RST(RST), .Dout(n30bmem_1_dout));
  _30bMem u_30bmem_2 (
    .ADDR(ADDR[29:0]), .Din(Din), .str(demultiplexer_1_out1), .CLK(CLK), .RST(RST), .Dout(n30bmem_2_dout));
  _30bMem u_30bmem_3 (
    .ADDR(ADDR[29:0]), .Din(Din), .str(demultiplexer_1_out2), .CLK(CLK), .RST(RST), .Dout(n30bmem_3_dout));
  _30bMem u_30bmem_4 (
    .ADDR(ADDR[29:0]), .Din(Din), .str(demultiplexer_1_out3), .CLK(CLK), .RST(RST), .Dout(n30bmem_4_dout));
  Multiplexer #(.select(2), .width(32), .enable("false")) multiplexer_1 (
    .in0(n30bmem_1_dout), .in1(n30bmem_2_dout), .in2(n30bmem_3_dout), .in3(n30bmem_4_dout), .out(Dout),
    .sel(ADDR[31:30]));

  // Other names for the same wires on the sheet: LoAddr[29:0] = ADDR[29:0]; memSel[1:0] = ADDR[31:30];
  //   Data[31:0] = Din
endmodule

module bubbler (
  input  prevWrEn,
  input  [3:0] rs1,
  input  [3:0] rs2,
  input  [3:0] prevrd,
  output bubble
);

  wire comparator_1_eq, comparator_2_eq, or_1_out;

  Comparator #(.width(4)) comparator_1 (.a(rs1), .b(prevrd), .eq(comparator_1_eq));  // open: gt, lt
  Comparator #(.width(4)) comparator_2 (.a(rs2), .b(prevrd), .eq(comparator_2_eq));  // open: gt, lt
  and and_1 (bubble, prevWrEn, or_1_out);
  or or_1 (or_1_out, comparator_1_eq, comparator_2_eq);
endmodule

// IO
module IoControl (
  input  [31:0] ABus,
  input  [31:0] DBus,
  input  WE,
  input  [9:0] SW,
  input  [3:0] KEYS,
  input  RST,
  output [31:0] DBus_2,
  output [7:0] LEDG,
  output [9:0] LEDR,
  output [15:0] HEX
);

  LEDG ledg_1 (.DATA(DBus), .WE(WE), .ADDR(ABus), .RST(RST), .LED(LEDG), .DATA_2(DBus_2));
  LEDR ledr_1 (.DATA(DBus), .WE(WE), .ADDR(ABus), .RST(RST), .LED(LEDR), .DATA_2(DBus_2));
  HEX hex_1 (.DATA(DBus), .WE(WE), .ADDR(ABus), .RST(RST), .HEX(HEX), .DATA_2(DBus_2));
  SW sw_1 (.DATA(DBus), .Switches(SW), .WE(WE), .ADDR(ABus), .RST(RST), .DATA_2(DBus_2));
  KEY key_1 (.DATA(DBus), .Keys(KEYS), .WE(WE), .ADDR(ABus), .RST(RST), .DATA_2(DBus_2));
  Timer timer_1 (.dBus(DBus), .aBus(ABus), .we(WE), .dBus_2(DBus_2));
endmodule

module LEDG (
  input  [31:0] DATA,
  input  WE,
  input  [31:0] ADDR,
  input  RST,
  output [7:0] LED,
  output [31:0] DATA_2
);

  wire and_1_out, comparator_1_eq;
  wire [31:0] bit_extender_1_out;

  Comparator #(.width(32), .mode("unsigned")) comparator_1 (
    .a(ADDR), .b(32'hf0000008), .eq(comparator_1_eq));  // open: gt, lt
  and and_1 (and_1_out, WE, comparator_1_eq);
  Register register_1 (.D(DATA[7:0]), .en(and_1_out), .Q(LED), .clk(and_1_out), .clr(RST));
  Multiplexer #(.width(32), .enable("false")) multiplexer_1 (
    .in1(bit_extender_1_out), .out(DATA_2), .sel(comparator_1_eq));  // open: in0
  assign bit_extender_1_out = {{24{1'b0}}, LED};  // Bit_Extender bit_extender_1
endmodule

module LEDR (
  input  [31:0] DATA,
  input  WE,
  input  [31:0] ADDR,
  input  RST,
  output [9:0] LED,
  output [31:0] DATA_2
);

  wire and_1_out, comparator_1_eq;
  wire [31:0] bit_extender_1_out;

  Comparator #(.width(32), .mode("unsigned")) comparator_1 (
    .a(ADDR), .b(32'hf0000004), .eq(comparator_1_eq));  // open: gt, lt
  and and_1 (and_1_out, WE, comparator_1_eq);
  Register #(.width(10)) register_1 (.D(DATA[9:0]), .en(and_1_out), .Q(LED), .clk(and_1_out), .clr(RST));
  assign bit_extender_1_out = {{22{1'b0}}, LED};  // Bit_Extender bit_extender_1
  Multiplexer #(.width(32), .enable("false")) multiplexer_1 (
    .in1(bit_extender_1_out), .out(DATA_2), .sel(comparator_1_eq));  // open: in0
endmodule

module HEX (
  input  [31:0] DATA,
  input  WE,
  input  [31:0] ADDR,
  input  RST,
  output [15:0] HEX,
  output [31:0] DATA_2
);

  wire and_1_out, comparator_1_eq;
  wire [31:0] bit_extender_1_out;

  Comparator #(.width(32), .mode("unsigned")) comparator_1 (
    .a(ADDR), .b(32'hf0000000), .eq(comparator_1_eq));  // open: gt, lt
  and and_1 (and_1_out, WE, comparator_1_eq);
  Register #(.width(16)) register_1 (.D(DATA[15:0]), .en(and_1_out), .Q(HEX), .clk(and_1_out), .clr(RST));
  assign bit_extender_1_out = {{16{1'b0}}, HEX};  // Bit_Extender bit_extender_1
  Multiplexer #(.width(32), .enable("false")) multiplexer_1 (
    .in1(bit_extender_1_out), .out(DATA_2), .sel(comparator_1_eq));  // open: in0
endmodule

module SW (
  input  [31:0] DATA,
  input  [9:0] Switches,
  input  WE,
  input  [31:0] ADDR,
  input  RST,
  output [31:0] DATA_2
);

  wire and_1_out, and_2_out, comparator_1_eq, comparator_2_eq, comparator_3_eq, or_1_out;
  wire [1:0] not_1_out;
  wire [7:0] register_2_q;
  wire [9:0] register_1_q;
  wire [31:0] bit_extender_1_out, bit_extender_2_out;

  Comparator #(.width(32), .mode("unsigned")) comparator_1 (
    .a(ADDR), .b(32'hf0000014), .eq(comparator_1_eq));  // open: gt, lt
  Comparator #(.width(32), .mode("unsigned")) comparator_2 (
    .a(ADDR), .b(32'hf0000114), .eq(comparator_2_eq));  // open: gt, lt
  Register #(.width(10)) register_1 (.D(Switches), .en(1'b1), .Q(register_1_q), .clk(not_1_out[0]), .clr(RST));
  and and_1 (and_1_out, ~WE, comparator_1_eq);  // AND_Gate
  and and_2 (and_2_out, ~WE, comparator_2_eq);  // AND_Gate
  not not_1 (not_1_out[0], comparator_3_eq);
  Comparator #(.width(10)) comparator_3 (.a(Switches), .b(register_1_q), .eq(comparator_3_eq));  // open: gt, lt
  Multiplexer #(.width(32), .enable("false")) multiplexer_1 (
    .in1(bit_extender_1_out), .out(DATA_2), .sel(and_1_out));  // open: in0
  assign bit_extender_1_out = {{22{1'b0}}, register_1_q};  // Bit_Extender bit_extender_1
  or or_1 (or_1_out, and_1_out, RST);
  Multiplexer #(.enable("false")) multiplexer_2 (.in0(1'b0), .in1(1'b1), .out(not_1_out[1]), .sel(register_2_q[0]));
  Register register_2 (.D({{6{1'b0}}, not_1_out}), .en(1'b1), .Q(register_2_q), .clk(not_1_out[0]), .clr(or_1_out));
  Multiplexer #(.width(32), .enable("false")) multiplexer_3 (
    .in1(bit_extender_2_out), .out(DATA_2), .sel(and_2_out));  // open: in0
  assign bit_extender_2_out = {{24{1'b0}}, register_2_q};  // Bit_Extender bit_extender_2
endmodule

module KEY (
  input  [31:0] DATA,
  input  [3:0] Keys,
  input  WE,
  input  [31:0] ADDR,
  input  RST,
  output [31:0] DATA_2
);

  wire and_1_out, and_2_out, comparator_1_eq, comparator_2_eq, comparator_3_eq, or_1_out;
  wire [1:0] not_1_out;
  wire [3:0] register_1_q;
  wire [7:0] register_2_q;
  wire [31:0] bit_extender_1_out, bit_extender_2_out;

  Comparator #(.width(32), .mode("unsigned")) comparator_1 (
    .a(ADDR), .b(32'hf0000010), .eq(comparator_1_eq));  // open: gt, lt
  Comparator #(.width(32), .mode("unsigned")) comparator_2 (
    .a(ADDR), .b(32'hf0000110), .eq(comparator_2_eq));  // open: gt, lt
  Register #(.width(4)) register_1 (.D(Keys), .en(1'b1), .Q(register_1_q), .clk(not_1_out[0]), .clr(RST));
  and and_1 (and_1_out, ~WE, comparator_1_eq);  // AND_Gate
  and and_2 (and_2_out, ~WE, comparator_2_eq);  // AND_Gate
  not not_1 (not_1_out[0], comparator_3_eq);
  Comparator #(.width(4)) comparator_3 (.a(Keys), .b(register_1_q), .eq(comparator_3_eq));  // open: gt, lt
  Multiplexer #(.width(32), .enable("false")) multiplexer_1 (
    .in1(bit_extender_1_out), .out(DATA_2), .sel(and_1_out));  // open: in0
  assign bit_extender_1_out = {{28{1'b0}}, register_1_q};  // Bit_Extender bit_extender_1
  or or_1 (or_1_out, and_1_out, RST);
  Multiplexer #(.enable("false")) multiplexer_2 (.in0(1'b0), .in1(1'b1), .out(not_1_out[1]), .sel(register_2_q[0]));
  Register register_2 (.D({{6{1'b0}}, not_1_out}), .en(1'b1), .Q(register_2_q), .clk(not_1_out[0]), .clr(or_1_out));
  Multiplexer #(.width(32), .enable("false")) multiplexer_3 (
    .in1(bit_extender_2_out), .out(DATA_2), .sel(and_2_out));  // open: in0
  assign bit_extender_2_out = {{24{1'b0}}, register_2_q};  // Bit_Extender bit_extender_2
endmodule

module Timer (
  input  [31:0] dBus,
  input  [31:0] aBus,
  input  we,
  output [31:0] dBus_2
);

  wire and_1_out, and_2_out, and_4_out, and_5_out, and_6_out, and_7_out, clock_1_out, comparator_4_eq,
       comparator_4_lt, comparator_5_eq, or_1_out, TCNTADDR, TCTLADDR, TLIMADDR;
  wire [2:0] or_2_out;
  wire [8:0] multiplexer_2_out, TCTL_q;
  wire [31:0] adder_1_out, bit_extender_1_out, multiplexer_1_out, TCNT_q, TLIM_q;

  Comparator #(.width(32)) comparator_1 (.a(aBus), .b(32'hf0000020), .eq(TLIMADDR));  // open: gt, lt
  Comparator #(.width(32)) comparator_2 (.a(aBus), .b(32'hf0000024), .eq(TCNTADDR));  // open: gt, lt
  Comparator #(.width(32)) comparator_3 (.a(aBus), .b(32'hf0000120), .eq(TCTLADDR));  // open: gt, lt
  and and_1 (and_1_out, we, TLIMADDR);
  Adder #(.width(32)) adder_1 (.a(TCNT_q), .b(32'h1), .out(adder_1_out));  // open: cin, cout
  Multiplexer #(.width(32), .enable("false")) multiplexer_1 (
    .in0(adder_1_out), .in1({32{1'b0}}), .out(multiplexer_1_out), .sel(or_1_out));
  Register #(.width(32)) TLIM (.D(dBus), .en(and_1_out), .Q(TLIM_q), .clk(clock_1_out));  // open: clr
  Register #(.width(32)) TCNT (.D(multiplexer_1_out), .en(clock_1_out), .Q(TCNT_q), .clk(clock_1_out));  // open: clr
  Clock clock_1 (.out(clock_1_out));
  Comparator #(.width(32), .mode("unsigned")) comparator_4 (
    .a(TLIM_q), .b(TCNT_q), .eq(comparator_4_eq), .lt(comparator_4_lt));  // open: gt
  buf or_1 (or_1_out, comparator_4_eq);  // OR_Gate
  and and_2 (and_2_out, TCTLADDR, we);
  and and_3 (or_2_out[2], 1'b1, TCTL_q[0]);
  or or_2 (or_2_out[0], or_1_out, TCTL_q[0]);
  Multiplexer #(.width(9), .enable("false")) multiplexer_2 (
    .in0({{6{1'b0}}, or_2_out[2], 1'b0, or_2_out[0]}), .in1({9{1'b0}}), .out(multiplexer_2_out),
    .sel(and_4_out));
  and and_4 (and_4_out, and_2_out, comparator_5_eq);
  Comparator #(.width(3)) comparator_5 (.a(dBus[2:0]), .b(3'b000), .eq(comparator_5_eq));  // open: gt, lt
  Register #(.width(9)) TCTL (.D(multiplexer_2_out), .en(1'b1), .Q(TCTL_q), .clk(clock_1_out));  // open: clr
  and and_5 (and_5_out, ~we, TLIMADDR);  // AND_Gate
  and and_6 (and_6_out, ~we, TCNTADDR);  // AND_Gate
  assign bit_extender_1_out = {{23{1'b0}}, TCTL_q};  // Bit_Extender bit_extender_1
  Multiplexer #(.width(32), .enable("false")) multiplexer_3 (.in1(TLIM_q), .out(dBus_2), .sel(and_5_out));  // open: in0
  Multiplexer #(.width(32), .enable("false")) multiplexer_4 (.in1(TCNT_q), .out(dBus_2), .sel(and_6_out));  // open: in0
  Multiplexer #(.width(32), .enable("false")) multiplexer_5 (
    .in1(bit_extender_1_out), .out(dBus_2), .sel(and_7_out));  // open: in0
  and and_7 (and_7_out, ~we, TCTLADDR);  // AND_Gate
endmodule

// CLKDivider
module ClkDivider (
  input  CLK,
  input  RST,
  output out_3
);

  wire comparator_1_eq, not_1_out;
  wire [31:0] adder_1_out, multiplexer_1_out, register_1_q;

  Adder #(.width(32)) adder_1 (.a(register_1_q), .b(32'h1), .out(adder_1_out));  // open: cin, cout
  Multiplexer #(.width(32), .enable("false")) multiplexer_1 (
    .in0(adder_1_out), .in1({32{1'b0}}), .out(multiplexer_1_out), .sel(comparator_1_eq));
  Register #(.width(32)) register_1 (.D(multiplexer_1_out), .en(CLK), .Q(register_1_q), .clk(CLK), .clr(RST));
  Comparator #(.width(32)) comparator_1 (.a(32'ha), .b(register_1_q), .eq(comparator_1_eq));  // open: gt, lt
  not not_1 (not_1_out, out_3);
  Register #(.width(1)) register_2 (.D(not_1_out), .en(comparator_1_eq), .Q(out_3), .clk(CLK), .clr(RST));
endmodule
